// Logisim project Control_sequencer_Circuit.circ as structural Verilog: 12 circuits, main circuit main
module main (
  input  in_1,
  input  in_2,
  input  [7:0] in_3,
  input  in_4,
  input  in_5,
  input  in_6,
  output [7:0] out_7,
  output [7:0] out_8,
  output [3:0] out_9,
  output out_10,
  output [7:0] out_11,
  output [7:0] out_12,
  output [7:0] out_13,
  output [7:0] out_14,
  output [7:0] out_15,
  output [7:0] out_16,
  output [7:0] out_17,
  output [7:0] out_18,
  output [7:0] out_19,
  output [7:0] out_20,
  output [3:0] out_21,
  output [7:0] out_22,
  output [3:0] out_23,
  output [7:0] out_24,
  output [7:0] out_25,
  output [7:0] out_26,
  output [7:0] out_27,
  output [7:0] out_28,
  output [7:0] out_29,
  output [7:0] out_30,
  output [7:0] out_31,
  output [7:0] out_32,
  output [7:0] out_33,
  output [7:0] out_34
);

  wire a_in, a_out, alu_out_en, alu_sub, b_in, b_out, c_s_1_mar_in_en, controlled_buffer_2_out, fin_out, hlt,
       ins_reg_in_en, ins_reg_out_en, mar_in_en, not_1_out, pc_enn, pc_out_en, sram_rd;

  pc pc_1 (.pc_en(pc_enn), .pc_clk(in_4), .pc_reset(in_6), .pc_out_en(pc_out_en), .pc_value(out_9), .pc_out(out_21));
  s_ram s_ram_1 (
    .sram_rd(sram_rd), .sram_wr(in_1), .sram_d_in({out_34[7:4], out_21}), .mar_d_in({out_34[7:4], out_21}),
    .mar_in_en(mar_in_en), .sram_clk(in_4), .sram_d_out({out_34[7:4], out_21}), .out_8(out_16),
    .out_9(out_17), .out_10(out_18), .out_11(out_19), .out_12(out_20), .out_13(out_22), .out_14(out_24),
    .out_15(out_25), .out_16(out_26), .out_17(out_27), .out_18(out_28), .out_19(out_29), .out_20(out_30),
    .out_21(out_31), .out_22(out_32), .out_23(out_33));
  assign {out_34[7:4], out_21} = in_2 ? in_3 : 8'bz;  // Controlled_Buffer controlled_buffer_1
  not not_1 (not_1_out, in_2);
  reg_gp Reg_A (
    .reg_in({out_34[7:4], out_21}), .reg_in_en(a_in), .reg_clk(in_4), .reg_out_en(a_out),
    .reg_int_out(out_7), .reg_out(out_8));
  reg_gp Reg_B (
    .reg_in({out_34[7:4], out_21}), .reg_in_en(b_in), .reg_clk(in_4), .reg_out_en(b_out),
    .reg_int_out(out_12), .reg_out(out_13));
  ins_reg ins_reg_1 (
    .ins_reg_in({out_34[7:4], out_21}), .ins_reg_in_en(ins_reg_in_en), .clk(in_4),
    .ins_reg_out_en(ins_reg_out_en), .add_outs(out_21), .ins_out(out_23));
  assign controlled_buffer_2_out = not_1_out ? in_4 : 1'bz;  // Controlled_Buffer controlled_buffer_2
  aluu aluu_1 (
    .alu_in_1(out_7), .alu_out_en(alu_out_en), .alu_sub(alu_sub), .alu_in_2(out_12), .alu_carry_out(out_10),
    .alu_out(out_11));
  assign mar_in_en = in_2 ? in_5 : 1'bz;  // Controlled_Buffer controlled_buffer_3
  c_s c_s_1 (
    .clk(controlled_buffer_2_out), .reset(in_6), .D(out_23[3]), .C(out_23[2]), .B(out_23[1]), .A(out_23[0]),
    .pc_out_en(not_1_out), .ins_reg_in_en(not_1_out), .mar_in_enn(not_1_out), .ins_reg_out_en(not_1_out),
    .a_out_en(not_1_out), .a_in(not_1_out), .alu_out_en(not_1_out), .b_in(not_1_out), .b_out_en(not_1_out),
    .pc_enn(not_1_out), .HLT(hlt), .pc_out(pc_out_en), .ins_reg_in(ins_reg_in_en), .pc_en(pc_enn),
    .mar_in_en(c_s_1_mar_in_en), .sram_rd(sram_rd), .ins_reg_out(ins_reg_out_en), .a_out(a_out),
    .alu_sub(alu_sub), .reg_in(a_in), .alu_out(alu_out_en), .reg_in_b(b_in), .b_out(b_out), .fin_out(fin_out));
  reg_gp Output_reg (
    .reg_in(out_11), .reg_in_en(alu_out_en), .reg_clk(in_4), .reg_out_en(fin_out), .reg_int_out(out_14),
    .reg_out(out_15));
  buf buffer_1 (mar_in_en, c_s_1_mar_in_en);

  assign out_34[3:0] = out_21;

  // Other names for the same wires on the sheet: clk = in_4; debug = in_2; debug_data[7:0] = in_3; pc_reset = in_6;
  //   sram_wr = in_1
endmodule

module reg_gp (
  input  [7:0] reg_in,
  input  reg_in_en,
  input  reg_clk,
  input  reg_out_en,
  output [7:0] reg_int_out,
  output [7:0] reg_out
);

  wire multiplexer_1_out, multiplexer_2_out, multiplexer_3_out, multiplexer_4_out, multiplexer_5_out,
       multiplexer_6_out, multiplexer_7_out, multiplexer_8_out;

  Multiplexer multiplexer_1 (.in0(reg_int_out[7]), .in1(reg_in[7]), .out(multiplexer_1_out), .sel(reg_in_en));
  D_Flip_Flop d_ff_1 (.D(multiplexer_1_out), .clk(reg_clk), .Q(reg_int_out[7]));  // open: Qn, preset, reset
  assign reg_out[7] = reg_out_en ? reg_int_out[7] : 1'bz;  // Controlled_Buffer controlled_buffer_1
  Multiplexer multiplexer_2 (.in0(reg_int_out[6]), .in1(reg_in[6]), .out(multiplexer_2_out), .sel(reg_in_en));
  D_Flip_Flop d_ff_2 (.D(multiplexer_2_out), .clk(reg_clk), .Q(reg_int_out[6]));  // open: Qn, preset, reset
  assign reg_out[6] = reg_out_en ? reg_int_out[6] : 1'bz;  // Controlled_Buffer controlled_buffer_2
  Multiplexer multiplexer_3 (.in0(reg_int_out[5]), .in1(reg_in[5]), .out(multiplexer_3_out), .sel(reg_in_en));
  D_Flip_Flop d_ff_3 (.D(multiplexer_3_out), .clk(reg_clk), .Q(reg_int_out[5]));  // open: Qn, preset, reset
  assign reg_out[5] = reg_out_en ? reg_int_out[5] : 1'bz;  // Controlled_Buffer controlled_buffer_3
  Multiplexer multiplexer_4 (.in0(reg_int_out[4]), .in1(reg_in[4]), .out(multiplexer_4_out), .sel(reg_in_en));
  D_Flip_Flop d_ff_4 (.D(multiplexer_4_out), .clk(reg_clk), .Q(reg_int_out[4]));  // open: Qn, preset, reset
  Multiplexer multiplexer_5 (.in0(reg_int_out[3]), .in1(reg_in[3]), .out(multiplexer_5_out), .sel(reg_in_en));
  assign reg_out[4] = reg_out_en ? reg_int_out[4] : 1'bz;  // Controlled_Buffer controlled_buffer_4
  D_Flip_Flop d_ff_5 (.D(multiplexer_5_out), .clk(reg_clk), .Q(reg_int_out[3]));  // open: Qn, preset, reset
  assign reg_out[3] = reg_out_en ? reg_int_out[3] : 1'bz;  // Controlled_Buffer controlled_buffer_5
  Multiplexer multiplexer_6 (.in0(reg_int_out[2]), .in1(reg_in[2]), .out(multiplexer_6_out), .sel(reg_in_en));
  D_Flip_Flop d_ff_6 (.D(multiplexer_6_out), .clk(reg_clk), .Q(reg_int_out[2]));  // open: Qn, preset, reset
  assign reg_out[2] = reg_out_en ? reg_int_out[2] : 1'bz;  // Controlled_Buffer controlled_buffer_6
  Multiplexer multiplexer_7 (.in0(reg_int_out[1]), .in1(reg_in[1]), .out(multiplexer_7_out), .sel(reg_in_en));
  D_Flip_Flop d_ff_7 (.D(multiplexer_7_out), .clk(reg_clk), .Q(reg_int_out[1]));  // open: Qn, preset, reset
  assign reg_out[1] = reg_out_en ? reg_int_out[1] : 1'bz;  // Controlled_Buffer controlled_buffer_7
  Multiplexer multiplexer_8 (.in0(reg_int_out[0]), .in1(reg_in[0]), .out(multiplexer_8_out), .sel(reg_in_en));
  D_Flip_Flop d_ff_8 (.D(multiplexer_8_out), .clk(reg_clk), .Q(reg_int_out[0]));  // open: Qn, preset, reset
  assign reg_out[0] = reg_out_en ? reg_int_out[0] : 1'bz;  // Controlled_Buffer controlled_buffer_8
endmodule

module aluu (
  input  [7:0] alu_in_1,
  input  alu_out_en,
  input  alu_sub,
  input  [7:0] alu_in_2,
  output alu_carry_out,
  output [7:0] alu_out
);

  wire adder_2_cout, adder_3_cout, adder_4_cout, adder_5_cout, adder_6_cout, adder_7_cout, adder_8_cout,
       xor_1_out, xor_2_out, xor_3_out, xor_4_out, xor_5_out, xor_6_out, xor_7_out, xor_8_out;
  wire [7:0] adder_8_out;

  xor xor_1 (xor_1_out, alu_in_2[7], alu_sub);
  Adder #(.width(1)) adder_1 (
    .a(alu_in_1[7]), .b(xor_1_out), .out(adder_8_out[7]), .cin(adder_2_cout), .cout(alu_carry_out));
  xor xor_2 (xor_2_out, alu_in_2[6], alu_sub);
  Adder #(.width(1)) adder_2 (
    .a(alu_in_1[6]), .b(xor_2_out), .out(adder_8_out[6]), .cin(adder_3_cout), .cout(adder_2_cout));
  xor xor_3 (xor_3_out, alu_in_2[5], alu_sub);
  Adder #(.width(1)) adder_3 (
    .a(alu_in_1[5]), .b(xor_3_out), .out(adder_8_out[5]), .cin(adder_4_cout), .cout(adder_3_cout));
  xor xor_4 (xor_4_out, alu_in_2[4], alu_sub);
  Adder #(.width(1)) adder_4 (
    .a(alu_in_1[4]), .b(xor_4_out), .out(adder_8_out[4]), .cin(adder_5_cout), .cout(adder_4_cout));
  xor xor_5 (xor_5_out, alu_in_2[3], alu_sub);
  Adder #(.width(1)) adder_5 (
    .a(alu_in_1[3]), .b(xor_5_out), .out(adder_8_out[3]), .cin(adder_6_cout), .cout(adder_5_cout));
  xor xor_6 (xor_6_out, alu_in_2[2], alu_sub);
  Adder #(.width(1)) adder_6 (
    .a(alu_in_1[2]), .b(xor_6_out), .out(adder_8_out[2]), .cin(adder_7_cout), .cout(adder_6_cout));
  xor xor_7 (xor_7_out, alu_in_2[1], alu_sub);
  Adder #(.width(1)) adder_7 (
    .a(alu_in_1[1]), .b(xor_7_out), .out(adder_8_out[1]), .cin(adder_8_cout), .cout(adder_7_cout));
  xor xor_8 (xor_8_out, alu_in_2[0], alu_sub);
  Adder #(.width(1)) adder_8 (.a(alu_in_1[0]), .b(xor_8_out), .out(adder_8_out[0]), .cin(alu_sub), .cout(adder_8_cout));
  assign alu_out = alu_out_en ? adder_8_out : 8'bz;  // Controlled_Buffer controlled_buffer_1
endmodule

module pc (
  input  pc_en,
  input  pc_clk,
  input  pc_reset,
  input  pc_out_en,
  output [3:0] pc_value,
  output [3:0] pc_out
);

  wire j_k_ff_2_qn, j_k_ff_3_qn, j_k_ff_4_qn;

  J_K_Flip_Flop j_k_ff_1 (
    .J(pc_en), .K(pc_en), .clk(j_k_ff_2_qn), .Q(pc_value[3]), .reset(pc_reset));  // open: Qn, preset
  J_K_Flip_Flop j_k_ff_2 (
    .J(pc_en), .K(pc_en), .clk(j_k_ff_3_qn), .Q(pc_value[2]), .Qn(j_k_ff_2_qn), .reset(pc_reset));  // open: preset
  J_K_Flip_Flop j_k_ff_3 (
    .J(pc_en), .K(pc_en), .clk(j_k_ff_4_qn), .Q(pc_value[1]), .Qn(j_k_ff_3_qn), .reset(pc_reset));  // open: preset
  J_K_Flip_Flop j_k_ff_4 (
    .J(pc_en), .K(pc_en), .clk(pc_clk), .Q(pc_value[0]), .Qn(j_k_ff_4_qn), .reset(pc_reset));  // open: preset
  assign pc_out = pc_out_en ? pc_value : 4'bz;  // Controlled_Buffer controlled_buffer_1
endmodule

module dec_4x16 (
  input  [3:0] dec_sel,
  output [15:0] dec_out
);

  wire not_1_out, not_2_out, not_3_out, not_4_out;

  not not_1 (not_1_out, dec_sel[3]);
  not not_2 (not_2_out, dec_sel[2]);
  not not_3 (not_3_out, dec_sel[1]);
  not not_4 (not_4_out, dec_sel[0]);
  and and_1 (dec_out[0], not_4_out, not_3_out, not_2_out, not_1_out);
  and and_2 (dec_out[1], dec_sel[0], not_3_out, not_2_out, not_1_out);
  and and_3 (dec_out[2], not_4_out, dec_sel[1], not_2_out, not_1_out);
  and and_4 (dec_out[3], dec_sel[0], dec_sel[1], not_2_out, not_1_out);
  and and_5 (dec_out[4], not_4_out, not_3_out, dec_sel[2], not_1_out);
  and and_6 (dec_out[5], dec_sel[0], not_3_out, dec_sel[2], not_1_out);
  and and_7 (dec_out[6], not_4_out, dec_sel[1], dec_sel[2], not_1_out);
  and and_8 (dec_out[7], dec_sel[0], dec_sel[1], dec_sel[2], not_1_out);
  and and_9 (dec_out[8], not_4_out, not_3_out, not_2_out, dec_sel[3]);
  and and_10 (dec_out[9], dec_sel[0], not_3_out, not_2_out, dec_sel[3]);
  and and_11 (dec_out[10], not_4_out, dec_sel[1], not_2_out, dec_sel[3]);
  and and_12 (dec_out[11], dec_sel[0], dec_sel[1], not_2_out, dec_sel[3]);
  and and_13 (dec_out[12], not_4_out, not_3_out, dec_sel[2], dec_sel[3]);
  and and_14 (dec_out[13], dec_sel[0], not_3_out, dec_sel[2], dec_sel[3]);
  and and_15 (dec_out[14], not_4_out, dec_sel[1], dec_sel[2], dec_sel[3]);
  and and_16 (dec_out[15], dec_sel[0], dec_sel[1], dec_sel[2], dec_sel[3]);
endmodule

module sram_cell (
  input  [7:0] data_in,
  input  wr_en,
  input  clk,
  input  cs,
  input  rd_en,
  output [7:0] memory_content,
  output [7:0] data_out
);

  wire and_1_out, and_2_out;

  and and_1 (and_1_out, wr_en, cs);
  and and_2 (and_2_out, cs, rd_en);
  reg_gp reg_gp_1 (
    .reg_in(data_in), .reg_in_en(and_1_out), .reg_clk(clk), .reg_out_en(and_2_out),
    .reg_int_out(memory_content), .reg_out(data_out));
endmodule

module s_ram (
  input  sram_rd,
  input  sram_wr,
  input  [7:0] sram_d_in,
  input  [7:0] mar_d_in,
  input  mar_in_en,
  input  sram_clk,
  output [7:0] sram_d_out,
  output [7:0] out_8,
  output [7:0] out_9,
  output [7:0] out_10,
  output [7:0] out_11,
  output [7:0] out_12,
  output [7:0] out_13,
  output [7:0] out_14,
  output [7:0] out_15,
  output [7:0] out_16,
  output [7:0] out_17,
  output [7:0] out_18,
  output [7:0] out_19,
  output [7:0] out_20,
  output [7:0] out_21,
  output [7:0] out_22,
  output [7:0] out_23
);

  wire [7:0] controlled_buffer_1_out, reg_gp_1_reg_int_out;
  wire [15:0] dec_4x16_1_dec_out;

  reg_gp reg_gp_1 (
    .reg_in(mar_d_in), .reg_in_en(mar_in_en), .reg_clk(sram_clk), .reg_int_out(reg_gp_1_reg_int_out));  // open: reg_out_en, reg_out
  dec_4x16 dec_4x16_1 (.dec_sel(reg_gp_1_reg_int_out[3:0]), .dec_out(dec_4x16_1_dec_out));
  assign controlled_buffer_1_out = sram_wr ? sram_d_in : 8'bz;  // Controlled_Buffer controlled_buffer_1
  sram_cell sram_cell_1 (
    .data_in(controlled_buffer_1_out), .wr_en(sram_wr), .clk(sram_clk), .cs(dec_4x16_1_dec_out[0]),
    .rd_en(sram_rd), .memory_content(out_8), .data_out(controlled_buffer_1_out));
  sram_cell sram_cell_2 (
    .data_in(controlled_buffer_1_out), .wr_en(sram_wr), .clk(sram_clk), .cs(dec_4x16_1_dec_out[1]),
    .rd_en(sram_rd), .memory_content(out_9), .data_out(controlled_buffer_1_out));
  sram_cell sram_cell_3 (
    .data_in(controlled_buffer_1_out), .wr_en(sram_wr), .clk(sram_clk), .cs(dec_4x16_1_dec_out[2]),
    .rd_en(sram_rd), .memory_content(out_10), .data_out(controlled_buffer_1_out));
  sram_cell sram_cell_4 (
    .data_in(controlled_buffer_1_out), .wr_en(sram_wr), .clk(sram_clk), .cs(dec_4x16_1_dec_out[3]),
    .rd_en(sram_rd), .memory_content(out_11), .data_out(controlled_buffer_1_out));
  sram_cell sram_cell_5 (
    .data_in(controlled_buffer_1_out), .wr_en(sram_wr), .clk(sram_clk), .cs(dec_4x16_1_dec_out[4]),
    .rd_en(sram_rd), .memory_content(out_12), .data_out(controlled_buffer_1_out));
  sram_cell sram_cell_6 (
    .data_in(controlled_buffer_1_out), .wr_en(sram_wr), .clk(sram_clk), .cs(dec_4x16_1_dec_out[5]),
    .rd_en(sram_rd), .memory_content(out_13), .data_out(controlled_buffer_1_out));
  sram_cell sram_cell_7 (
    .data_in(controlled_buffer_1_out), .wr_en(sram_wr), .clk(sram_clk), .cs(dec_4x16_1_dec_out[6]),
    .rd_en(sram_rd), .memory_content(out_14), .data_out(controlled_buffer_1_out));
  sram_cell sram_cell_8 (
    .data_in(controlled_buffer_1_out), .wr_en(sram_wr), .clk(sram_clk), .cs(dec_4x16_1_dec_out[7]),
    .rd_en(sram_rd), .memory_content(out_15), .data_out(controlled_buffer_1_out));
  sram_cell sram_cell_9 (
    .data_in(controlled_buffer_1_out), .wr_en(sram_wr), .clk(sram_clk), .cs(dec_4x16_1_dec_out[8]),
    .rd_en(sram_rd), .memory_content(out_16), .data_out(controlled_buffer_1_out));
  sram_cell sram_cell_10 (
    .data_in(controlled_buffer_1_out), .wr_en(sram_wr), .clk(sram_clk), .cs(dec_4x16_1_dec_out[9]),
    .rd_en(sram_rd), .memory_content(out_17), .data_out(controlled_buffer_1_out));
  sram_cell sram_cell_11 (
    .data_in(controlled_buffer_1_out), .wr_en(sram_wr), .clk(sram_clk), .cs(dec_4x16_1_dec_out[10]),
    .rd_en(sram_rd), .memory_content(out_18), .data_out(controlled_buffer_1_out));
  sram_cell sram_cell_12 (
    .data_in(controlled_buffer_1_out), .wr_en(sram_wr), .clk(sram_clk), .cs(dec_4x16_1_dec_out[11]),
    .rd_en(sram_rd), .memory_content(out_19), .data_out(controlled_buffer_1_out));
  sram_cell sram_cell_13 (
    .data_in(controlled_buffer_1_out), .wr_en(sram_wr), .clk(sram_clk), .cs(dec_4x16_1_dec_out[12]),
    .rd_en(sram_rd), .memory_content(out_20), .data_out(controlled_buffer_1_out));
  sram_cell sram_cell_14 (
    .data_in(controlled_buffer_1_out), .wr_en(sram_wr), .clk(sram_clk), .cs(dec_4x16_1_dec_out[13]),
    .rd_en(sram_rd), .memory_content(out_21), .data_out(controlled_buffer_1_out));
  sram_cell sram_cell_15 (
    .data_in(controlled_buffer_1_out), .wr_en(sram_wr), .clk(sram_clk), .cs(dec_4x16_1_dec_out[14]),
    .rd_en(sram_rd), .memory_content(out_22), .data_out(controlled_buffer_1_out));
  sram_cell sram_cell_16 (
    .data_in(controlled_buffer_1_out), .wr_en(sram_wr), .clk(sram_clk), .cs(dec_4x16_1_dec_out[15]),
    .rd_en(sram_rd), .memory_content(out_23), .data_out(controlled_buffer_1_out));
  assign sram_d_out = sram_rd ? controlled_buffer_1_out : 8'bz;  // Controlled_Buffer controlled_buffer_2
endmodule

module ins_reg (
  input  [7:0] ins_reg_in,
  input  ins_reg_in_en,
  input  clk,
  input  ins_reg_out_en,
  output [3:0] add_outs,
  output [3:0] ins_out
);

  wire [3:0] reg_gp_1_reg_int_out;

  reg_gp reg_gp_1 (
    .reg_in(ins_reg_in), .reg_in_en(ins_reg_in_en), .reg_clk(clk),
    .reg_int_out({ins_out, reg_gp_1_reg_int_out}));  // open: reg_out_en, reg_out
  assign add_outs = ins_reg_out_en ? reg_gp_1_reg_int_out : 4'bz;  // Controlled_Buffer controlled_buffer_1
endmodule

module layout (
  input  in_1,
  input  in_2,
  input  in_3,
  input  in_4,
  input  in_5,
  input  in_6,
  input  in_7,
  input  in_8,
  input  in_9,
  input  in_10,
  input  in_11,
  input  in_12,
  input  in_13,
  input  in_14,
  input  in_15,
  input  in_16,
  input  [7:0] in_17,
  output [7:0] out_18,
  output [7:0] out_19,
  output [7:0] out_20,
  output [7:0] out_21,
  output [7:0] out_22,
  output [7:0] out_23,
  output [3:0] out_24,
  output [7:0] out_25,
  output [3:0] out_26,
  output [7:0] out_27,
  output [7:0] out_28,
  output [7:0] out_29,
  output [7:0] out_30,
  output [7:0] out_31,
  output [7:0] out_32,
  output [7:0] out_33,
  output [7:0] out_34,
  output [7:0] out_35,
  output [7:0] out_36,
  output [7:0] out_37
);

  wire debug;
  wire [7:0] reg_gp_1_reg_out, reg_gp_2_reg_int_out;

  pc pc_1 (.pc_en(in_12), .pc_clk(in_15), .pc_reset(in_14), .pc_out_en(in_13), .pc_value(out_24));  // open: pc_out
  s_ram s_ram_1 (
    .sram_rd(in_8), .sram_wr(in_9), .sram_d_in({out_37[7:4], out_24}), .mar_d_in({out_37[7:4], out_24}),
    .mar_in_en(in_7), .sram_clk(in_15), .sram_d_out({out_37[7:4], out_24}), .out_8(out_19), .out_9(out_20),
    .out_10(out_21), .out_11(out_22), .out_12(out_23), .out_13(out_25), .out_14(out_27), .out_15(out_28),
    .out_16(out_29), .out_17(out_30), .out_18(out_31), .out_19(out_32), .out_20(out_33), .out_21(out_34),
    .out_22(out_35), .out_23(out_36));
  assign {out_37[7:4], out_24} = debug ? in_17 : 8'bz;  // Controlled_Buffer controlled_buffer_1
  reg_gp reg_gp_1 (
    .reg_in({out_37[7:4], out_24}), .reg_in_en(in_1), .reg_clk(in_15), .reg_out_en(in_2),
    .reg_int_out(out_18), .reg_out(reg_gp_1_reg_out));
  reg_gp reg_gp_2 (
    .reg_in({out_37[7:4], out_24}), .reg_in_en(in_1), .reg_clk(in_15), .reg_out_en(in_2),
    .reg_int_out(reg_gp_2_reg_int_out), .reg_out(reg_gp_1_reg_out));
  ins_reg ins_reg_1 (
    .ins_reg_in({out_37[7:4], out_24}), .ins_reg_in_en(in_10), .clk(in_15), .ins_reg_out_en(in_11),
    .add_outs(out_24), .ins_out(out_26));
  aluu aluu_1 (
    .alu_in_1(out_18), .alu_out_en(in_5), .alu_sub(in_6), .alu_in_2(reg_gp_2_reg_int_out),
    .alu_out({out_37[7:4], out_24}));  // open: alu_carry_out

  assign out_37[3:0] = out_24;

  // Other names for the same wires on the sheet: a_in = in_1; a_out = in_2; alu_out = in_5; alu_sub = in_6;
  //   b_in = in_3; b_out = in_4; clk = in_15; debug_data[7:0] = in_17; degub = in_16; ins_reg_in_en = in_10;
  //   ins_reg_out_en = in_11; mar_in_en = in_7; pc_en = in_12; pc_out = in_13; pc_reset = in_14; sram_rd = in_8;
  //   sram_wr = in_9
endmodule

module ring_c (
  input  clk,
  input  reset,
  output T1,
  output T2,
  output T3,
  output T4,
  output T5,
  output T6
);

  wire nor_1_out;

  D_Flip_Flop d_ff_1 (.D(nor_1_out), .clk(clk), .Q(T1), .reset(reset));  // open: Qn, preset
  nor nor_1 (nor_1_out, T6, T5, T4, T3, T2, T1);
  D_Flip_Flop d_ff_2 (.D(T1), .clk(clk), .Q(T2), .reset(reset));  // open: Qn, preset
  D_Flip_Flop d_ff_3 (.D(T2), .clk(clk), .Q(T3), .reset(reset));  // open: Qn, preset
  D_Flip_Flop d_ff_4 (.D(T3), .clk(clk), .Q(T4), .reset(reset));  // open: Qn, preset
  D_Flip_Flop d_ff_5 (.D(T4), .clk(clk), .Q(T5), .reset(reset));  // open: Qn, preset
  D_Flip_Flop d_ff_6 (.D(T5), .clk(clk), .Q(T6), .reset(reset));  // open: Qn, preset
endmodule

module ins_dec (
  input  D,
  input  C,
  input  B,
  input  A,
  output LDA,
  output LDB,
  output ADD,
  output O_UT,
  output SUB,
  output HLT
);

  wire not_1_out, not_2_out, not_3_out, not_4_out;

  not not_1 (not_1_out, D);
  not not_2 (not_2_out, C);
  not not_3 (not_3_out, B);
  not not_4 (not_4_out, A);
  and and_1 (LDA, not_1_out, not_2_out, not_3_out, A);
  and and_2 (LDB, not_1_out, not_2_out, B, not_4_out);
  and and_3 (ADD, not_1_out, C, B, A);
  and and_4 (O_UT, D, not_2_out, not_3_out, not_4_out);
  and and_5 (SUB, D, C, not_3_out, not_4_out);
  and and_6 (HLT, not_1_out, C, not_3_out, not_4_out);
endmodule

module c_s (
  input  clk,
  input  reset,
  input  D,
  input  C,
  input  B,
  input  A,
  input  pc_out_en,
  input  ins_reg_in_en,
  input  mar_in_enn,
  input  ins_reg_out_en,
  input  a_out_en,
  input  a_in,
  input  alu_out_en,
  input  b_in,
  input  b_out_en,
  input  pc_enn,
  output HLT,
  output pc_out,
  output ins_reg_in,
  output pc_en,
  output mar_in_en,
  output sram_rd,
  output ins_reg_out,
  output a_out,
  output alu_sub,
  output reg_in,
  output alu_out,
  output reg_in_b,
  output b_out,
  output fin_out
);

  wire and_1_out, and_2_out, and_3_out, and_4_out, and_5_out, and_6_out, and_7_out, and_8_out, and_9_out,
       and_11_out, and_12_out, and_13_out, ins_dec_1_add, ins_dec_1_lda, ins_dec_1_ldb, ins_dec_1_o_ut,
       ins_dec_1_sub, or_1_out, or_3_out, or_4_out, ring_c_1_t1, ring_c_1_t2, ring_c_1_t3, ring_c_1_t4,
       ring_c_1_t5, ring_c_1_t6;

  ring_c ring_c_1 (
    .clk(clk), .reset(reset), .T1(ring_c_1_t1), .T2(ring_c_1_t2), .T3(ring_c_1_t3), .T4(ring_c_1_t4),
    .T5(ring_c_1_t5), .T6(ring_c_1_t6));
  ins_dec ins_dec_1 (
    .D(D), .C(C), .B(B), .A(A), .LDA(ins_dec_1_lda), .LDB(ins_dec_1_ldb), .ADD(ins_dec_1_add),
    .O_UT(ins_dec_1_o_ut), .SUB(ins_dec_1_sub), .HLT(HLT));
  assign pc_out = pc_out_en ? ring_c_1_t1 : 1'bz;  // Controlled_Buffer controlled_buffer_1
  assign ins_reg_in = ins_reg_in_en ? ring_c_1_t2 : 1'bz;  // Controlled_Buffer controlled_buffer_2
  assign pc_en = pc_enn ? ring_c_1_t3 : 1'bz;  // Controlled_Buffer controlled_buffer_3
  and and_1 (and_1_out, ins_dec_1_lda, ring_c_1_t4);
  or or_1 (or_1_out, ring_c_1_t1, and_1_out, and_5_out, and_7_out, and_3_out);
  assign mar_in_en = mar_in_enn ? or_1_out : 1'bz;  // Controlled_Buffer controlled_buffer_4
  and and_2 (and_2_out, ins_dec_1_lda, ring_c_1_t5);
  or or_2 (sram_rd, ring_c_1_t2, and_2_out, and_6_out, and_4_out, and_8_out);
  and and_3 (and_3_out, ins_dec_1_ldb, ring_c_1_t4);
  or or_3 (or_3_out, and_1_out, and_5_out, and_7_out, and_3_out);
  assign ins_reg_out = ins_reg_out_en ? or_3_out : 1'bz;  // Controlled_Buffer controlled_buffer_5
  and and_4 (and_4_out, ins_dec_1_ldb, ring_c_1_t5);
  and and_5 (and_5_out, ins_dec_1_add, ring_c_1_t4);
  and and_6 (and_6_out, ins_dec_1_add, ring_c_1_t5);
  and and_7 (and_7_out, ins_dec_1_sub, ring_c_1_t4);
  and and_8 (and_8_out, ins_dec_1_sub, ring_c_1_t5);
  and and_9 (and_9_out, ins_dec_1_o_ut, ring_c_1_t4);
  assign a_out = a_out_en ? and_9_out : 1'bz;  // Controlled_Buffer controlled_buffer_6
  and and_10 (alu_sub, ins_dec_1_sub, ring_c_1_t5);
  assign reg_in = a_in ? and_2_out : 1'bz;  // Controlled_Buffer controlled_buffer_7
  and and_11 (and_11_out, ins_dec_1_add, ring_c_1_t5);
  and and_12 (and_12_out, ins_dec_1_sub, ring_c_1_t5);
  or or_4 (or_4_out, and_11_out, and_12_out);
  assign alu_out = alu_out_en ? or_4_out : 1'bz;  // Controlled_Buffer controlled_buffer_8
  assign reg_in_b = b_in ? and_4_out : 1'bz;  // Controlled_Buffer controlled_buffer_9
  and and_13 (and_13_out, ins_dec_1_o_ut, ring_c_1_t4);
  assign b_out = b_out_en ? and_13_out : 1'bz;  // Controlled_Buffer controlled_buffer_10
  and and_14 (fin_out, ins_dec_1_o_ut, ring_c_1_t4);
endmodule
